# Fritzing sketch Sketch (saved by Fritzing 0.9.10b)
breadboards: 1

parts:
  WeMos_D1_Mini1 = WeMos D1 Mini
  Part1 = Analog Digital MUX Breakout
  Part2 = Analog Digital MUX Breakout
  7_Segment2 = 7 Segment Display
  7_Segment3 = 7 Segment Display
  Part3 = LED Tactile Button Breakout v10 [part_number=BOB-10467]
  Part4 = LED Tactile Button Breakout v10 [part_number=BOB-10467]

nets:
  VCC: WeMos_D1_Mini1.5V, Part1.VCC, Part2.VCC, 7_Segment2.common_cathode, 7_Segment3.common_cathode, Part3.2, Part4.2, Part4.4
  N1: WeMos_D1_Mini1.D0, Part3.4
  N2: WeMos_D1_Mini1.D2, Part1.S2
  N3: WeMos_D1_Mini1.D3, Part1.S1
  N4: WeMos_D1_Mini1.D4, Part1.S0
  N5: WeMos_D1_Mini1.D5, Part2.SIG
  N6: WeMos_D1_Mini1.D6, Part2.S2
  N7: WeMos_D1_Mini1.D7, Part2.S1
  N8: WeMos_D1_Mini1.D8, Part2.S0
  GND: WeMos_D1_Mini1.G, Part1.GND, Part2.GND, Part3.1, Part4.1
  N9: WeMos_D1_Mini1.RX, Part3.3
  N10: WeMos_D1_Mini1.TX, Part4.3
  N11: Part1.C0, 7_Segment2.Segment_A
  N12: Part1.C1, 7_Segment2.Segment_B
  N13: Part1.C2, 7_Segment2.Segment_G
  N14: Part1.C3, 7_Segment2.Segment_F
  N15: Part1.C4, 7_Segment2.Segment_C
  N16: Part1.C5, 7_Segment2.Segment_D
  N17: Part1.C6, 7_Segment2.Segment_E
  N18: Part2.C0, 7_Segment3.Segment_A
  N19: Part2.C1, 7_Segment3.Segment_B
  N20: Part2.C2, 7_Segment3.Segment_G
  N21: Part2.C3, 7_Segment3.Segment_F
  N22: Part2.C4, 7_Segment3.Segment_C
  N23: Part2.C5, 7_Segment3.Segment_D
  N24: Part2.C6, 7_Segment3.Segment_E

custom parts:
  WeMos D1 Mini: The D1 mini is a mini wifi board based on ESP-8266EX.
